// Logisim project lab2a.circ as structural Verilog: 4 circuits, main circuit Main (DO NOT MODIFY)
module Main__DO_NOT_MODIFY (
);

  wire _6_Bit_Enable, _8_Bit_Enable, Clock, comparator_1_eq, comparator_2_eq, comparator_3_eq,
       counter_1_carry, counter_2_carry, n3_fsm_implementation_1_q, rom_2_data, rom_4_data;
  wire [3:0] n2_register_implementation_1_d0, register_1_q, rom_1_data;
  wire [5:0] _6_Bit_Counter;
  wire [6:0] adder_1_out, adder_2_out, adder_3_out, bit_extender_1_out, bit_extender_2_out,
       bit_extender_3_out;
  wire [7:0] _8_Bit_Counter, Your_Data;
  wire [11:0] rom_3_data;

  Clock clock_1 (.out(Clock));
  Counter #(.ongoal("stay")) counter_1 (
    .count(1'b1), .Q(_8_Bit_Counter), .carry(counter_1_carry), .clk(Clock));  // open: load, D, clr
  not not_1 (_8_Bit_Enable, counter_1_carry);
  Counter #(.width(6), .max('h3f), .ongoal("stay")) counter_2 (
    .count(1'b1), .Q(_6_Bit_Counter), .carry(counter_2_carry), .clk(Clock));  // open: load, D, clr
  not not_2 (_6_Bit_Enable, counter_2_carry);
  ROM #(.addrWidth(6), .dataWidth(4)) rom_1 (.addr(_6_Bit_Counter), .data(rom_1_data));  // open: sel
  ROM #(.addrWidth(6), .dataWidth(1)) rom_2 (.addr(_6_Bit_Counter), .data(rom_2_data));  // open: sel
  ROM #(.dataWidth(12)) rom_3 (.addr(_8_Bit_Counter), .data(rom_3_data));  // open: sel
  _1_Error_correcting u_1_error_correcting_1 (
    .D7(rom_3_data[11]), .D6(rom_3_data[10]), .D5(rom_3_data[9]), .D4(rom_3_data[8]), .D3(rom_3_data[6]),
    .D2(rom_3_data[5]), .D1(rom_3_data[4]), .D0(rom_3_data[2]), .C3(rom_3_data[7]), .C2(rom_3_data[3]),
    .C1(rom_3_data[1]), .C0(rom_3_data[0]), .Z7(Your_Data[7]), .Z6(Your_Data[6]), .Z5(Your_Data[5]),
    .Z4(Your_Data[4]), .Z3(Your_Data[3]), .Z2(Your_Data[2]), .Z1(Your_Data[1]), .Z0(Your_Data[0]));
  _2_Register_implementation u_2_register_implementation_1 (
    .I3(rom_1_data[3]), .I2(rom_1_data[2]), .I1(rom_1_data[1]), .I0(rom_1_data[0]), .Clock(Clock),
    .D3(n2_register_implementation_1_d0[3]), .D2(n2_register_implementation_1_d0[2]),
    .D1(n2_register_implementation_1_d0[1]), .Enable(_6_Bit_Enable), .D0(n2_register_implementation_1_d0[0]));
  _3_FSM_implementation u_3_fsm_implementation_1 (
    .w(rom_2_data), .Clock(Clock), .Q(n3_fsm_implementation_1_q), .Enable(_6_Bit_Enable));
  // Probe on {rom_3_data[11:8], rom_3_data[6:4], rom_3_data[2]}
  // Probe on _8_Bit_Counter
  // Probe on Your_Data
  ROM #(.addrWidth(6), .dataWidth(1)) rom_4 (.addr(_6_Bit_Counter), .data(rom_4_data));  // open: sel
  Register #(.width(4)) register_1 (.D(rom_1_data), .en(_6_Bit_Enable), .Q(register_1_q), .clk(Clock));  // open: clr
  Comparator #(.mode("unsigned")) comparator_1 (
    .a(Your_Data), .b(_8_Bit_Counter), .eq(comparator_1_eq));  // open: gt, lt
  Comparator #(.width(4), .mode("unsigned")) comparator_2 (
    .a(n2_register_implementation_1_d0), .b(register_1_q), .eq(comparator_2_eq));  // open: gt, lt
  Comparator #(.width(1), .mode("unsigned")) comparator_3 (
    .a(n3_fsm_implementation_1_q), .b(rom_4_data), .eq(comparator_3_eq));  // open: gt, lt
  assign bit_extender_1_out = {{6{1'b0}}, comparator_1_eq};  // Bit_Extender bit_extender_1
  assign bit_extender_2_out = {{6{1'b0}}, comparator_2_eq};  // Bit_Extender bit_extender_2
  Adder #(.width(7)) adder_1 (.a(bit_extender_2_out), .b(7'b0110000), .out(adder_1_out));  // open: cin, cout
  assign bit_extender_3_out = {{6{1'b0}}, comparator_3_eq};  // Bit_Extender bit_extender_3
  Adder #(.width(7)) adder_2 (.a(bit_extender_3_out), .b(7'b0110000), .out(adder_2_out));  // open: cin, cout
  Adder #(.width(7)) adder_3 (.a(bit_extender_1_out), .b(7'b0110000), .out(adder_3_out));  // open: cin, cout
  TTY tty_1 (.data(adder_3_out), .clk(Clock), .we(_8_Bit_Enable));  // open: clr
  TTY #(.cols(8)) tty_2 (.data(adder_1_out), .clk(Clock), .we(_6_Bit_Enable));  // open: clr
  TTY #(.cols(8)) tty_3 (.data(adder_2_out), .clk(Clock), .we(_6_Bit_Enable));  // open: clr
  // Probe on comparator_2_eq
  // Probe on comparator_3_eq
  // Probe on comparator_1_eq

  // Notes on the sheet:
  //   contents of rom_1 (hex, n*v repeats v):
  //   6 b 3 c 9 b 2 8 3 7 9 c 4 1 f 8 e d 2 6 9 6 2 0 d 8 2 5 a 4 c 9 2 1 a 3 b 6 e f e 2 c a c 6 c a 4 6
  //   a 4 f c 7 5 6 6 7 b 7 4 1 6
  //   contents of rom_2 (hex, n*v repeats v):
  //   0 4*1 0 0 0 4*1 0 1 1 0 0 1 5*0 1 1 1 0 0 0 1 5*0 1 0 1 0 0 1 0 1 1 0 0 5*1 4*0 1 5*0 1
  //   contents of rom_3 (hex, n*v repeats v):
  //   1 f 219 11e aa 2d 33 b4 24b 4c 56 55 61 66 78 7f 181 18e 198 19f 1ab 1ac 1b2 9b5 1ca 1cd 1d3 1d4 1e2
  //   1e7 1f9 3fe 282 285 29b 39c 2b8 2af 2f1 3b6 2c9 2ce 2d8 2d7 6e3 2ec 2fa 2fd 303 304 31a 31d 329 32e
  //   330 337 348 35f 359 356 362 367 b7b 37c 483 684 49a 49d 4a9 4ae 4b8 4b7 4c8 4cf 4d1 4d6 6e2 4e5 4fb
  //   4fc 506 545 53b 51c 528 52f 531 536 549 54e 552 d57 563 d64 57a 57d e01 686 618 71f 62f 62c 632 6b5
  //   64a 64d 653 e54 660 6e7 6f9 67e 780 f87 7d9 79e 7aa 7bd 7b3 7b4 7eb 7cd 7d2 7d5 7e1 7e6 7f8 7ff 8c8
  //   88f c91 996 8aa 8a5 cbb 8fc 8c3 8c4 8da 8dd ce9 8ee 8f2 8f7 909 90e 911 917 923 924 93a 93d 942 b45
  //   b5b 95c 96a 96f 971 9f6 a0a a0d a13 a14 a30 a37 a39 a3e e41 a46 a5a a5f a6b a6c a72 b75 bab b8c b92
  //   b95 ba1 ba6 bb8 bbf bc0 bc7 bd9 bfe bea bed bfb bf4 c0b c0e c12 c55 ca1 d26 c38 c3f c50 c47 c59 c7e
  //   c6a c6d c73 c74 d8a f8d d93 d94 da8 da7 db9 dfe dc3 dce df8 ddf deb dec df2 df5 e89 e8e e92 eb7 ea3
  //   ea4 ebb ebd ec2 ee5 edb edc eec eef ef1 ef6 f0c f0f f31 f16 f22 f35 f3b fbc f43 f4c f5a f7d f6d f6f
  //   f70 f77
  //   contents of rom_4 (hex, n*v repeats v):
  //   0 0 0 1 0 0 0 1 0 0 1 4*0 1 0 1 7*0 1 6*0 1 0 1 5*0 1 0 0 0 1 0 1 0 0 1 0 0 0 1 0 1
  //   All values in TTY will be 1 when correct, except for bottom right corner which will be empty
  //   Last input will be 1 as well
  //   All values in TTY will be 1 when correct, except for bottom right corner which will be empty
  //   Last input will be 1 as well
  //   All values in TTY will be 1 when correct, except for bottom right corner which will be empty
  //   Last input will be 1 as well
endmodule

module _1_Error_correcting (
  input  D7,
  input  D6,
  input  D5,
  input  D4,
  input  C3,
  input  D3,
  input  D2,
  input  D1,
  input  C2,
  input  D0,
  input  C1,
  input  C0,
  output Z7,
  output Z6,
  output Z5,
  output Z4,
  output Z3,
  output Z2,
  output Z1,
  output Z0
);
endmodule

module _2_Register_implementation (
  input  I3,
  input  I2,
  input  I1,
  input  I0,
  input  Clock,
  input  Enable,
  output D3,
  output D2,
  output D1,
  output D0
);
endmodule

module _3_FSM_implementation (
  input  w,
  input  Clock,
  input  Enable,
  output Q
);
endmodule
