// Logisim project lab2b.circ as structural Verilog: 5 circuits, main circuit Main (DO NOT MODIFY)
module Main__DO_NOT_MODIFY (
);

  wire _5_Bit_Enable, _6_Bit_Enable, Clock, comparator_1_eq, comparator_2_eq, comparator_3_eq,
       comparator_4_eq, comparator_5_eq, counter_1_carry, counter_2_carry, n4_bit_sequence_checker_1_r,
       n5_fsm_implementation_1_s, n6_parity_generator_1_t, rom_2_data, rom_3_data, rom_4_data, rom_5_data,
       rom_6_data, rom_7_data;
  wire [1:0] counter_3_q;
  wire [2:0] n7_vending_machine_fsm_1_o5, rom_1_data, rom_8_data;
  wire [4:0] counter_2_q;
  wire [5:0] _6_Bit_Counter;
  wire [6:0] adder_1_out, adder_2_out, adder_3_out, adder_4_out, bit_extender_1_out, bit_extender_2_out,
       bit_extender_3_out, bit_extender_4_out;

  Clock clock_1 (.out(Clock));
  Counter #(.width(6), .max('h3f), .ongoal("stay")) counter_1 (
    .Q(_6_Bit_Counter), .carry(counter_1_carry), .clk(Clock));  // open: load, D, count, clr
  not not_1 (_6_Bit_Enable, counter_1_carry);
  Counter #(.width(5), .max('h1f), .ongoal("stay")) counter_2 (
    .Q(counter_2_q), .carry(counter_2_carry), .clk(Clock));  // open: load, D, count, clr
  not not_2 (_5_Bit_Enable, counter_2_carry);
  ROM #(.addrWidth(6), .dataWidth(3)) rom_1 (.addr(_6_Bit_Counter), .data(rom_1_data));  // open: sel
  ROM #(.addrWidth(6), .dataWidth(1)) rom_2 (.addr(_6_Bit_Counter), .data(rom_2_data));  // open: sel
  ROM #(.addrWidth(6), .dataWidth(1)) rom_3 (.addr(_6_Bit_Counter), .data(rom_3_data));  // open: sel
  ROM #(.addrWidth(5), .dataWidth(1)) rom_4 (.addr(counter_2_q), .data(rom_4_data));  // open: sel
  Counter #(.width(2), .max('h2)) counter_3 (.Q(counter_3_q), .clk(Clock));  // open: load, D, count, carry, clr
  _4_Bit_sequence_checker u_4_bit_sequence_checker_1 (
    .x(rom_2_data), .Clock(Clock), .Enable(_6_Bit_Enable), .R(n4_bit_sequence_checker_1_r));
  _5_FSM_implementation u_5_fsm_implementation_1 (
    .y(rom_3_data), .Clock(Clock), .Enable(_6_Bit_Enable), .S(n5_fsm_implementation_1_s));
  _6_Parity_generator u_6_parity_generator_1 (
    .z(rom_4_data), .T(n6_parity_generator_1_t), .Enable(_5_Bit_Enable), .Clock(Clock));
  Comparator #(.width(2), .mode("unsigned")) comparator_1 (
    .a(counter_3_q), .b(2'b00), .eq(comparator_1_eq));  // open: gt, lt
  _7_Vending_machine_FSM u_7_vending_machine_fsm_1 (
    .I25(rom_1_data[2]), .I10(rom_1_data[1]), .I5(rom_1_data[0]), .Clock(Clock), .Enable(_6_Bit_Enable),
    .OM(n7_vending_machine_fsm_1_o5[2]), .O10(n7_vending_machine_fsm_1_o5[1]),
    .O5(n7_vending_machine_fsm_1_o5[0]));
  ROM #(.addrWidth(6), .dataWidth(1)) rom_5 (.addr(_6_Bit_Counter), .data(rom_5_data));  // open: sel
  ROM #(.addrWidth(6), .dataWidth(1)) rom_6 (.addr(_6_Bit_Counter), .data(rom_6_data));  // open: sel
  // Probe on rom_6_data
  // Probe on n5_fsm_implementation_1_s
  ROM #(.addrWidth(5), .dataWidth(1)) rom_7 (.addr(counter_2_q), .data(rom_7_data));  // open: sel
  Shift_Register #(.length(3)) shift_register_1 (
    .in(rom_4_data), .clk(Clock));  // open: shift, out, load, clr, d0, q0, d1, q1, d2, q2
  ROM #(.addrWidth(6), .dataWidth(3)) rom_8 (.addr(_6_Bit_Counter), .data(rom_8_data));  // open: sel
  Comparator #(.width(1)) comparator_2 (
    .a(n4_bit_sequence_checker_1_r), .b(rom_5_data), .eq(comparator_2_eq));  // open: gt, lt
  // Probe on rom_5_data
  // Probe on n4_bit_sequence_checker_1_r
  Comparator #(.width(1)) comparator_3 (
    .a(n5_fsm_implementation_1_s), .b(rom_6_data), .eq(comparator_3_eq));  // open: gt, lt
  Comparator #(.width(1)) comparator_4 (
    .a(n6_parity_generator_1_t), .b(rom_7_data), .eq(comparator_4_eq));  // open: gt, lt
  // Probe on n6_parity_generator_1_t
  // Probe on rom_7_data
  // Probe on comparator_1_eq
  // Probe on n7_vending_machine_fsm_1_o5[2]
  // Probe on n7_vending_machine_fsm_1_o5[1]
  // Probe on n7_vending_machine_fsm_1_o5[0]
  // Probe on rom_8_data[2]
  // Probe on rom_8_data[1]
  // Probe on rom_8_data[0]
  Comparator #(.width(3), .mode("unsigned")) comparator_5 (
    .a(n7_vending_machine_fsm_1_o5), .b(rom_8_data), .eq(comparator_5_eq));  // open: gt, lt
  assign bit_extender_1_out = {{6{1'b0}}, comparator_2_eq};  // Bit_Extender bit_extender_1
  Adder #(.width(7)) adder_1 (.a(bit_extender_1_out), .b(7'b0110000), .out(adder_1_out));  // open: cin, cout
  assign bit_extender_2_out = {{6{1'b0}}, comparator_3_eq};  // Bit_Extender bit_extender_2
  Adder #(.width(7)) adder_2 (.a(bit_extender_2_out), .b(7'b0110000), .out(adder_2_out));  // open: cin, cout
  assign bit_extender_3_out = {{6{1'b0}}, comparator_4_eq};  // Bit_Extender bit_extender_3
  assign bit_extender_4_out = {{6{1'b0}}, comparator_5_eq};  // Bit_Extender bit_extender_4
  TTY #(.cols(8)) tty_1 (.data(adder_1_out), .clk(Clock), .we(_6_Bit_Enable));  // open: clr
  TTY #(.cols(8)) tty_2 (.data(adder_2_out), .clk(Clock), .we(_6_Bit_Enable));  // open: clr
  Adder #(.width(7)) adder_3 (.a(bit_extender_3_out), .b(7'b0110000), .out(adder_3_out));  // open: cin, cout
  TTY #(.rows(4), .cols(8)) tty_3 (.data(adder_3_out), .clk(Clock), .we(_5_Bit_Enable));  // open: clr
  Adder #(.width(7)) adder_4 (.a(bit_extender_4_out), .b(7'b0110000), .out(adder_4_out));  // open: cin, cout
  TTY #(.cols(8)) tty_4 (.data(adder_4_out), .clk(Clock), .we(_6_Bit_Enable));  // open: clr
  // Probe on comparator_2_eq
  // Probe on comparator_3_eq
  // Probe on comparator_4_eq
  // Probe on comparator_5_eq

  // Notes on the sheet:
  //   4 = Quarter
  //   2 = Dime
  //   1 = Nickel
  //   contents of rom_1 (hex, n*v repeats v):
  //   8*1 2 1 1 2 1 1 2 1 1 2 1 1 1 2 2 1 2 1 2 1 2 2 4 2 2 2 1 2 1 2 1 1 2 2 1 4 2 4 1 2 4 2 2 4 2 1 1 4
  //   1 1 2 4 1 1 1 4
  //   contents of rom_2 (hex, n*v repeats v):
  //   0 1 0 1 0 1 1 1 0 1 0 0 1 1 4*0 1 0 1 0 1 0 0 1 0 4*1 4*0 1 1 0 0 1 1 0 0 0 1 1 0 1 0 0 1 1 0 1 1 1
  //   0 1 1 0 4*1
  //   contents of rom_3 (hex, n*v repeats v):
  //   0 1 0 1 0 1 1 1 0 1 0 0 1 1 4*0 1 0 1 0 1 0 0 1 0 4*1 4*0 1 1 0 0 1 1 0 0 0 1 1 0 1 0 0 1 1 0 1 1 1
  //   0 1 1 0 4*1
  //   contents of rom_4 (hex, n*v repeats v):
  //   5*0 1 0 1 0 0 1 1 1 0 0 1 0 1 1 1 0 4*1 0 1 0 1 1
  //   contents of rom_5 (hex, n*v repeats v):
  //   0 0 0 1 0 0 0 1 19*0 1 27*0 1
  //   contents of rom_6 (hex, n*v repeats v):
  //   0 1 0 1 0 1 0 0 1 1 0 1 1 0 1 0 1 0 1 0 1 0 1 0 1 1 0 1 0 1 0 1 1 0 1 0 1 0 1 0 1 0 1 0 1 0 0 1 0 1
  //   1 0 0 1 0 0 1 1 0 1 0 1
  //   contents of rom_7 (hex, n*v repeats v):
  //   6*0 1 0 0 1 5*0 1 8*0 1
  //   contents of rom_8 (hex, n*v repeats v):
  //   4*0 4 0 0 0 4 0 0 0 4 0 0 0 4 0 0 0 4 0 0 4 0 0 4 0 0 4 4 0 0 5 0 0 0 5 0 0 0 5 0 5 0 6 0 0 7 0 0 7
  //   0 0 0 7 0 0 0 7 0 0 0 7
  //   Shift register contains last 3 bits when 3 Bits Input probe is 1
  //   3 Bits Input probe will be 1 on initial clock cycle, ignore that
  //   TTY will be filled with all 1s when correct, except for bottom corner which will be empty
  //   Last input will also be 1
  //   TTY will be filled with all 1s when correct, except for bottom corner which will be empty
  //   Last input will also be 1
  //   TTY will be filled with all 1s when correct, except for bottom corner which will be empty
  //   Last input will also be 1
  //   TTY will be filled with all 1s when correct, except for bottom corner which will be empty
  //   Last input will also be 1
endmodule

module _4_Bit_sequence_checker (
  input  x,
  input  Clock,
  input  Enable,
  output R
);
endmodule

module _5_FSM_implementation (
  input  y,
  input  Clock,
  input  Enable,
  output S
);
endmodule

module _6_Parity_generator (
  input  z,
  input  Clock,
  input  Enable,
  output T
);
endmodule

module _7_Vending_machine_FSM (
  input  I25,
  input  I10,
  input  I5,
  input  Enable,
  input  Clock,
  output OM,
  output O5,
  output O10
);
endmodule
