// Logisim project lab3.circ as structural Verilog: 1 circuit, main circuit main
module main (
);

  wire clock_1_out, comparator_1_lt, counter_1_carry, not_1_out, Reset, TClock;
  wire [2:0] rom_1_data;
  wire [3:0] multiplexer_1_out;
  wire [4:0] MSB;
  wire [5:0] counter_1_q;
  wire [6:0] adder_1_out, LSB;
  wire [8:0] R0, R1, R2, R3, R4, R5, R6, R7;

  TTY #(.rows(33), .cols(1)) tty_1 (.data({2'b10, MSB}), .clk(TClock), .clr(Reset));  // open: we
  TTY #(.rows(33), .cols(1)) tty_2 (.data(LSB), .clk(TClock), .clr(Reset));  // open: we
  Button u_Reset (.out(Reset));
  Counter #(.width(6), .max('h20), .ongoal("stay")) counter_1 (
    .Q(counter_1_q), .carry(counter_1_carry), .clk(TClock), .clr(Reset));  // open: load, D, count
  Multiplexer #(.select(3), .width(9), .disabled(0), .enable("false")) multiplexer_1 (
    .in0(R0), .in1(R1), .in2(R2), .in3(R3), .in4(R4), .in5(R5), .in6(R6), .in7(R7),
    .out({MSB, multiplexer_1_out}), .sel(rom_1_data));
  not not_1 (not_1_out, counter_1_carry);
  Clock clock_1 (.out(clock_1_out));
  and and_1 (TClock, not_1_out, clock_1_out);
  ROM #(.addrWidth(6), .dataWidth(3)) rom_1 (.addr(counter_1_q), .data(rom_1_data));  // open: sel
  // Probe on {3'b011, multiplexer_1_out}
  // Probe on {2'b10, MSB}
  Comparator #(.width(7)) comparator_1 (
    .a(7'b0111001), .b({3'b011, multiplexer_1_out}), .lt(comparator_1_lt));  // open: gt, eq
  // Probe on LSB
  Multiplexer #(.width(7), .disabled(0), .enable("false")) multiplexer_2 (
    .in0({3'b011, multiplexer_1_out}), .in1(adder_1_out), .out(LSB), .sel(comparator_1_lt));
  Adder #(.width(7)) adder_1 (.a({3'b011, multiplexer_1_out}), .b(7'b0000111), .out(adder_1_out));  // open: cin, cout

  // Notes on the sheet:
  //   @0
  //   JA
  //   E5
  //   @0
  //   OF
  //   U5
  //   OF
  //   E5
  //   E5
  //   U4
  //   E5
  //   E5
  //   U4
  //   _F
  //   _F
  //   _F
  //   AF
  //   AF
  //   AF
  //   @0
  //   AE
  //   AE
  //   AE
  //   _E
  //   OF
  //   ^0
  //   J9
  //   P1
  //   R0
  //   R0
  //   ^0
  //   _F
  //   contents of rom_1 (hex, n*v repeats v):
  //   0 0 1 2 3 4 5 6 6 2 3 4 5 6 6 0 1 2 3 4 5 6 6 2 3 4 5 6 6 6 7
endmodule
